// Logisim project PS2Keyboard.circ as structural Verilog: 1 circuit, main circuit main
module main (
);

  wire ACK, and_1_out, and_2_out, and_3_out, and_4_out, and_6_out, buffer_1_out, buffer_2_out, d_ff_1_q,
       d_ff_2_q, d_ff_2_qn, DATA_LINE, IRQ, keyboard_1_avail, nand_1_out, nand_2_out, not_1_out, not_2_out,
       not_3_out, not_5_out, not_8_out, not_9_out, PS2_CLK, PS2_DATA, pull_resistor_1_node,
       pull_resistor_2_node, pull_resistor_4_node, pull_resistor_5_node, pull_resistor_8_node,
       pull_resistor_9_node, pull_resistor_11_node, pull_resistor_12_node, pull_resistor_13_node,
       pull_resistor_17_node, pull_resistor_18_node, pull_resistor_19_node, S1, S11, s_r_ff_1_q, SHIFT,
       shift_register_2_p1, shift_register_2_p3, SYS_CLK;
  wire [3:0] counter_1_q, counter_2_q, not_4_out;
  wire [6:0] keyboard_1_data, register_2_q;
  wire [7:0] KEYCODE, undriven;
  wire [7:7] pull_resistor_3_node, register_2_q_2;
  wire [11:0] pull_resistor_16_node;

  Keyboard keyboard_1 (
    .clk(SYS_CLK), .re(pull_resistor_2_node), .clr(pull_resistor_1_node), .avail(keyboard_1_avail),
    .data(keyboard_1_data));
  Pull_Resistor pull_resistor_1 (.node(pull_resistor_1_node));
  Pull_Resistor #(.pull(1)) pull_resistor_2 (.node(pull_resistor_2_node));
  // Digital_Oscilloscope #(.nState(16)) digital_oscilloscope_1: pin names not known; wires that end beside it: SYS_CLK, PS2_CLK, S1, S11, SHIFT, DATA_LINE, PS2_DATA
  Register register_1 (
    .D({pull_resistor_3_node[7], keyboard_1_data}), .en(pull_resistor_3_node[7]), .clk(keyboard_1_avail),
    .Q(KEYCODE));  // open: clr
  Pull_Resistor #(.pull(1)) pull_resistor_3 (.node(pull_resistor_3_node[7]));
  Hex_Digit_Display hex_digit_display_1 (.value(KEYCODE[7:4]));  // open: dp
  Clock clock_1 (.out(SYS_CLK));
  Hex_Digit_Display hex_digit_display_2 (.value(KEYCODE[3:0]));  // open: dp
  D_Flip_Flop d_ff_1 (
    .D(pull_resistor_4_node), .clk(keyboard_1_avail), .Q(d_ff_1_q), .reset(and_1_out));  // open: Qn, preset
  Pull_Resistor #(.pull(1)) pull_resistor_4 (.node(pull_resistor_4_node));
  and and_1 (and_1_out, d_ff_1_q, S1);
  S_R_Flip_Flop #(.trigger("high")) s_r_ff_1 (
    .S(d_ff_1_q), .R(S11), .clk(pull_resistor_5_node), .Q(s_r_ff_1_q));  // open: reset, Qn, preset
  Pull_Resistor #(.pull(1)) pull_resistor_5 (.node(pull_resistor_5_node));
  not not_1 (not_1_out, S1);
  not not_2 (not_2_out, DATA_LINE);
  and and_2 (and_2_out, s_r_ff_1_q, SYS_CLK);
  and and_3 (and_3_out, not_1_out, SHIFT);
  Pull_Resistor #(.pull(1)) pull_resistor_6 (.node(PS2_DATA));
  Transistor #(.\type ("n")) transistor_1 (.in(1'b0), .out(PS2_DATA), .gate(and_4_out));
  and and_4 (and_4_out, not_2_out, SHIFT);
  Pull_Resistor #(.pull(1)) pull_resistor_7 (.node(PS2_CLK));
  Transistor #(.\type ("n")) transistor_2 (.in(1'b0), .out(PS2_CLK), .gate(and_2_out));
  Counter #(.max('hf), .width(4)) counter_1 (
    .clr(S11), .load(pull_resistor_8_node), .up(pull_resistor_9_node), .count(s_r_ff_1_q), .clk(not_3_out),
    .Q(counter_1_q));  // open: D, carry
  Pull_Resistor pull_resistor_8 (.node(pull_resistor_8_node));
  Pull_Resistor #(.pull(1)) pull_resistor_9 (.node(pull_resistor_9_node));
  not not_3 (not_3_out, and_2_out);
  // Shift_Register shift_register_1: pin names not known; wires that end beside it: S11, S1, and_3_out, SYS_CLK, DATA_LINE
  Pull_Resistor pull_resistor_10 ();  // open: node
  buf buffer_1 (buffer_1_out, PS2_DATA);
  buf buffer_2 (buffer_2_out, PS2_CLK);
  assign not_4_out = ~counter_1_q;  // NOT_Gate not_4, 4 bits wide
  D_Flip_Flop d_ff_2 (
    .D(pull_resistor_11_node), .clk(not_5_out), .Q(d_ff_2_q), .Qn(d_ff_2_qn), .reset(and_6_out));  // open: preset
  Pull_Resistor #(.pull(1)) pull_resistor_11 (.node(pull_resistor_11_node));
  not not_5 (not_5_out, buffer_2_out);
  nand nand_1 (nand_1_out, counter_1_q[0], not_4_out[1], not_4_out[2], not_4_out[3]);
  not not_6 (S1, nand_1_out);
  nand nand_2 (nand_2_out, counter_1_q[0], counter_1_q[1], counter_1_q[3], not_4_out[2]);
  not not_7 (S11, nand_2_out);
  nand nand_3 (SHIFT, not_4_out[0], not_4_out[1], not_4_out[2], not_4_out[3]);
  Counter #(.max('hf), .width(4)) counter_2 (
    .clr(d_ff_2_qn), .load(pull_resistor_12_node), .up(pull_resistor_13_node), .count(d_ff_2_q),
    .clk(not_5_out), .Q(counter_2_q));  // open: D, carry
  Pull_Resistor pull_resistor_12 (.node(pull_resistor_12_node));
  Pull_Resistor #(.pull(1)) pull_resistor_13 (.node(pull_resistor_13_node));
  // Shift_Register #(.length(10)) shift_register_2: pin names not known; wires that end beside it: shift_register_2_p1, not_5_out, shift_register_2_p3
  Pull_Resistor pull_resistor_14 (.node(shift_register_2_p1));
  Pull_Resistor #(.pull(1)) pull_resistor_15 ();  // open: node
  and and_5 (shift_register_2_p3, buffer_1_out, d_ff_2_q);
  Pull_Resistor pull_resistor_16 (.node(pull_resistor_16_node));
  TTY tty_1 (.data(register_2_q), .clk(and_6_out), .we(pull_resistor_18_node), .clr(pull_resistor_17_node));
  Pull_Resistor pull_resistor_17 (.node(pull_resistor_17_node));
  Pull_Resistor #(.pull(1)) pull_resistor_18 (.node(pull_resistor_18_node));
  Register register_2 (
    .D(undriven), .en(pull_resistor_19_node), .clk(and_6_out), .Q({register_2_q_2[7], register_2_q}));  // open: clr
  Pull_Resistor #(.pull(1)) pull_resistor_19 (.node(pull_resistor_19_node));
  not not_8 (not_8_out, counter_2_q[0]);
  not not_9 (not_9_out, counter_2_q[2]);
  and and_6 (and_6_out, not_8_out, counter_2_q[1], not_9_out, counter_2_q[3]);
  S_R_Flip_Flop #(.trigger("high")) s_r_ff_2 (
    .S(and_6_out), .R(ACK), .clk(pull_resistor_19_node), .Q(IRQ));  // open: reset, Qn, preset
  Pull_Resistor pull_resistor_20 (.node(ACK));
  Hex_Digit_Display hex_digit_display_3 (.value({register_2_q_2[7], register_2_q[6:4]}));  // open: dp
  Hex_Digit_Display hex_digit_display_4 (.value(register_2_q[3:0]));  // open: dp
  Button button_1 (.out(ACK));

  // Notes on the sheet:
  //   Typed-In Key
  //   DEVICE (KEYBOARD/MOUSE) SIDE
  //   PRO TIP:
  //   RUN THIS SIM AT BELOW 256 HZ
  //   HOST (COMPUTER) SIDE
  //   Received Key
endmodule
